# Fritzing sketch Temperature_logger (saved by Fritzing 0.9.3b)
circuit board: 8.46667cm x 5.64444cm
breadboards: 1

parts:
  Composant1 = Arduino Nano (Rev3.0)
  Composant2 = MicroSD Card Module
  R1 = Resistor [tolerance=±5% resistance=47k package=THT]
  U1 = SWITCH-SPST-2 [package=r_sw_th]
  U2 = LIPO-2000mAh [package=lipo-2000]
  DS3 = DS18B20 1-Wire Temperature Sensor [part_number=DS18B20]
  DS2 = DS18B20 1-Wire Temperature Sensor [part_number=DS18B20]
  R2 = Resistor [tolerance=±5% resistance=220 package=THT]
  LED1 = smd LED [color="Red (633nm)" package="0805 [SMD]"]

nets:
  GND: Composant1.GND, Composant2.GND, U2.-, DS3.GND, DS2.GND, LED1.cathode
  N1: Composant1.D2, R1.Pin_1, DS3.DQ, DS2.DQ
  N2: Composant1.D4, Composant2.CS
  N3: Composant1.D7, R2.Pin_1
  N4: Composant1.D11/MOSI, Composant2.MOSI
  N5: Composant1.D12/MISO, Composant2.MISO
  N6: Composant1.VIN, U1.P
  VDD: Composant1.5V, Composant2.VCC, R1.Pin_0, DS3.VDD, DS2.VDD
  N7: Composant1.D13/SCK, Composant2.SCK
  N8: U1.O, U2.+
  N9: R2.Pin_0, LED1.anode

// code stored in the sketch: temperature_logger.ino
/*
  SD card temperature logger

  This log temperature from many DS18B20 sensors
  to an SD card using the SD library.
  In the mean time, it sends to the serial port the same info.

  The records are in CSV format, easing the use with spreadsheet programs.

  You can put nearly as many temperature sensors you want on the
  OneWire bus, all plugged in "parallel" with a single pullup resistor of 4,7k.

  The user can change the recording params in the configuration
  file that is automatically created on the SD card.

  An led is a visual confirmation of time between records.

  The circuit:
   sensors on analog pin 2
   SD card attached to SPI on dedicated port, but chip select is on pin 4
   The LED is on pin 7

  created  24 March 2017
  by patrick@brouille.net
*/

/**************************** User params default values ********************************/
unsigned long stepSec = 5;            // How many seconds between each record
unsigned long durationMin = 20;       // Max time for operation
unsigned long flashDuration;          // How long the LED will be on in milliseconds
String fileNamePrefix = "log";        // Temperature log file name prefix
int fileNameIndex = 1;                // Temperature log file name index to be incremented at each power up
String fileNameExtension = "csv";     // Temperature log file name extension

/********************************* Wiring pins ******************************************/
#define ONE_WIRE_BUS 2                // Data wire is plugged into port 2 on the Arduino
const int sdCardChipSelect = 4;       // SD card chip select is plugged into that pin number
const int ledPin = 7;                 // The number of the LED pin

/********************************** Libraries *******************************************/
#include <SPI.h>
#include <SD.h>
#include <OneWire.h>
#include <DallasTemperature.h>

/******************************* Other declarations *************************************/
String configFileName = "config.txt"; // The name of the config file on SD card
int deviceCount;                      // How many devices on the oneWire bus
File myFile;
unsigned long stepMil;                // X axis increase in milliseconds
unsigned long durationMil;            // Max recording duration in milliseconds
unsigned long durationCount;          // X axis for the temperature graph
unsigned long duration;               // duration is time limit for recording data, incremented at each new file
unsigned long currentMillis;          // To avoid delay()
unsigned long flashMil;               // The timestamp for LED ON
String fileName;

/******************************** init libraries *****************************************/
OneWire oneWire(ONE_WIRE_BUS);        // Setup a oneWire instance
DallasTemperature sensors(&oneWire);  // Pass our oneWire reference to Dallas Temperature.


void setup(void)
{
  // Start serial port
  Serial.begin(115200);

  // Start up the library
  sensors.begin();
  sensors.setResolution(12);

  // SD Card init
  Serial.print("Initializing SD card...");
  // See if the card is present and can be initialized:
  if (!SD.begin(sdCardChipSelect)) {
    Serial.println("Card failed, or not present");
    // Don't do anything more:
    return;
  }

  Serial.println("card initialized.");
  Serial.println("Waiting for user to push the button...");

  readSDSettings();
  writeSDSettings();

  // File name is built upon last file name
  //    ex.: last file "log8.csv" -> new file "log9.csv"
  fileName = fileNamePrefix + fileNameIndex + '.' + fileNameExtension;

  // Sensors
  deviceCount = sensors.getDeviceCount();
  Serial.print(deviceCount);
  Serial.println(" capteurs");

  pinMode(ledPin, OUTPUT);                // set the digital pin as output:

  // user params convertion
  stepMil = 1000L * stepSec;
  durationMil = 1000L * 60L * durationMin;
  durationCount = 0;
  duration = 0;
  currentMillis = 0;
  flashMil = 0;
}

void loop(void)
{
  /* 
   * Conditions for that loop: 
   *   - max time for recording not reached
   *   - at least the user step has elapsed (the X axis increase)
   */
  if (millis() < durationMil) {
    if (millis() > currentMillis) {

      // The flashing LED
      digitalWrite(ledPin, HIGH);         // turn LED ON

      // Call sensors.requestTemperatures() to issue a global temperature
      //     request for all devices on the bus
      sensors.requestTemperatures();
  
      // Make a string for assembling the data to log:
      String dataString = String(durationCount) + ",";
      for (byte index = 0; index < deviceCount; index++)
      {
        dataString += String(sensors.getTempCByIndex(index));
        if (index < (deviceCount - 1)) {
          dataString += ",";
        }
      }
  
      // Open the file. note that only one file can be open at a time,
      // so you have to close this one before opening another.
      File dataFile = SD.open(fileName, FILE_WRITE);
  
      // if the file is available, write to it:
      if (dataFile) {
        dataFile.println(dataString);
        dataFile.close();
        // print to the serial port too:
        Serial.println(dataString);
      }
      // If the file isn't open, pop up an error:
      else {
        Serial.println("error opening datalog.txt");
      }
  
      // Time related stuff
      durationCount += stepSec;           // Counter for X axis values
      currentMillis = millis() + stepMil; // Timer for temperature requests/records
      flashMil = millis() + flashDuration; // Timer for flash
    }

    // The flashing LED shall go off when timer ended
    if (millis() > flashMil) {
      digitalWrite(ledPin, LOW);          // turn LED OFF
    }
  }
}

void readSDSettings()
{
  char character;
  String settingName;
  String settingValue;
  myFile = SD.open(configFileName);
  if (myFile) {
    while (myFile.available()) {
      character = myFile.read();
      while ((myFile.available()) && (character != '[')) {
        character = myFile.read();
      }
      character = myFile.read();
      while ((myFile.available()) && (character != '=')) {
        settingName += character;
        character = myFile.read();
      }
      character = myFile.read();
      while ((myFile.available()) && (character != ']')) {
        settingValue = settingValue + character;
        character = myFile.read();
      }
      if (character == ']') {
        // Apply the value to the parameter
        if (settingName == "fileNamePrefix") {
          fileNamePrefix = settingValue;
        }
        if (settingName == "fileNameIndex") {
          fileNameIndex = settingValue.toInt() + 1;
        }
        if (settingName == "fileNameExtension") {
          fileNameExtension = settingValue;
        }
        if (settingName == "stepSec") {
          stepSec = toLong(settingValue);
        }
        if (settingName == "durationMin") {
          durationMin = toLong(settingValue);
        }
        if (settingName == "flashDuration") {
          flashDuration = toLong(settingValue);
        }
        // Reset Strings
        settingName = "";
        settingValue = "";
      }
    }
    // Close the file:
    myFile.close();
  } else {
    // If the file didn't open, print an info to the user
    // the configuration file will be created by writeSDSettings() later on
    Serial.print("no configuration file on the SD card... creating one");
  }
}

long toLong(String settingValue) {
  char longbuf[settingValue.length() + 1];
  settingValue.toCharArray(longbuf, sizeof(longbuf));
  long l = atol(longbuf);
  return l;
}

// Write a configuration file
void writeSDSettings()
{
  // Delete the old One
  SD.remove(configFileName);
  // Create new one
  myFile = SD.open(configFileName, FILE_WRITE);
  // Writing in the file works just like regular print()/println() function
  myFile.print("[fileNamePrefix=");
  myFile.print(fileNamePrefix);
  myFile.println("]");
  myFile.print("[fileNameIndex=");
  myFile.print(fileNameIndex);
  myFile.println("]");
  myFile.print("[fileNameExtension=");
  myFile.print(fileNameExtension);
  myFile.println("]");
  myFile.print("[stepSec=");
  myFile.print(stepSec);
  myFile.println("]");
  myFile.print("[durationMin=");
  myFile.print(durationMin);
  myFile.println("]");
  myFile.print("[flashDuration=");
  myFile.print(flashDuration);
  myFile.println("]");
  // Close the file:
  myFile.close();
  //Serial.println("Writing done.");
}
