# Fritzing sketch 1.09 (saved by Fritzing 0.9.3b)
breadboards: 1

parts:
  Part1 = Arduino Mega ADK (Rev3)
  R1 = Resistor [tolerance=±5% resistance=330 package=THT]
  i2C_16x2_LCD_Screen = IC, SIP package, 4 pins [chip_label="i2C 2x16 LCD"]
  MicroSD_Card_Reader = IC, SIP package, 6 pins [chip_label="MicroSD Card Reader"]
  RFID_Scanner = IC, SIP package, 8 pins [chip_label="RFID Scanner"]
  Real_Time_Clock = IC, SIP package, 6 pins [chip_label="Real Time Clock"]
  Fingerprint_Scanner = IC, SIP package, 4 pins [chip_label="Fingerprint Scanner"]
  LED1 = LED - 3mm [color="Red (633nm)" package="3 mm [THT]"]
  Left_Button = SIP - 2 pins [chip_label="Left Button" package="SIP (Single Inline) [THT]"]
  Back_Button = SIP - 2 pins [chip_label="Back Button" package="SIP (Single Inline) [THT]"]
  Enter_Button = SIP - 2 pins [chip_label="Enter Button" package="SIP (Single Inline) [THT]"]
  Right_Button = SIP - 2 pins [chip_label="Right Button" package="SIP (Single Inline) [THT]"]
  R2 = Resistor [tolerance=±5% resistance=220 package=THT]
  R4 = Resistor [tolerance=±5% resistance=330 package=THT]
  Solenoid = Solenoid
  Hall_Effect_Sensor_A3144 = IC, SIP package, 3 pins [chip_label="Hall Effect Sensor A3144"]
  R5 = Resistor [tolerance=±5% resistance=10k package=THT]
  Toggle_Switch = IC, SIP package, 5 pins [chip_label="Toggle Switch"]
  5V_(Dropped_from_Wall_outlet) = DC Power [voltage=5]
  Output_12V = Mini-360 DC-DC Buck converter [package=THT]
  MOSFET = Basic FET N-Channel [package="TO220 [THT]"]

nets:
  N1: Part1.A0, Hall_Effect_Sensor_A3144.pin3, R5.Pin_1
  N2: Part1.D21/SCL, i2C_16x2_LCD_Screen.pin4, Real_Time_Clock.pin3
  N3: Part1.D20/SDA, i2C_16x2_LCD_Screen.pin3, Real_Time_Clock.pin4
  N4: Part1.D19/RX1, Fingerprint_Scanner.pin2
  N5: Part1.D18/TX1, Fingerprint_Scanner.pin3
  N6: Part1.5V, R1.Pin_1, i2C_16x2_LCD_Screen.pin2, MicroSD_Card_Reader.pin2, Real_Time_Clock.pin5, Fingerprint_Scanner.pin1, R4.Pin_1, Hall_Effect_Sensor_A3144.pin1, R5.Pin_0
  N7: Part1.GND, i2C_16x2_LCD_Screen.pin1, MicroSD_Card_Reader.pin1, RFID_Scanner.pin6, Real_Time_Clock.pin6, Fingerprint_Scanner.pin4, Left_Button.pin2, Back_Button.pin2, Enter_Button.pin2, Right_Button.pin2, R2.Pin_1, Solenoid.pin1, Hall_Effect_Sensor_A3144.pin2, Toggle_Switch.pin1, Toggle_Switch.pin4, 5V_(Dropped_from_Wall_outlet).V-, Output_12V.IN-, Output_12V.OUT-
  N8: Part1.3V3, RFID_Scanner.pin8
  N9: Part1.VIN, Toggle_Switch.pin2, Toggle_Switch.pin5, Output_12V.IN+
  N10: Part1.D22, R1.Pin_0, RFID_Scanner.pin1
  N11: Part1.D23, RFID_Scanner.pin7
  N12: Part1.D24, LED1.anode
  N13: Part1.D25, MicroSD_Card_Reader.pin6, R4.Pin_0
  N14: Part1.D26, MOSFET.gate
  N15: Part1.D46, Left_Button.pin1
  N16: Part1.D47, Enter_Button.pin1
  N17: Part1.D48, Right_Button.pin1
  N18: Part1.D49, Back_Button.pin1
  N19: Part1.D50/MISO, MicroSD_Card_Reader.pin3, RFID_Scanner.pin4
  N20: Part1.D51/MOSI, MicroSD_Card_Reader.pin4, RFID_Scanner.pin3
  N21: Part1.D52/SCK, MicroSD_Card_Reader.pin5, RFID_Scanner.pin2
  N22: LED1.cathode, R2.Pin_0
  N23: Solenoid.pin2, MOSFET.source
  N24: Toggle_Switch.pin3, 5V_(Dropped_from_Wall_outlet).V+
  N25: Output_12V.OUT+, MOSFET.drain

custom parts:
  Mini-360 DC-DC Buck converter: Mini-360 DC-DC Buck converter. Tiny buck step down voltage converter, input voltage 4.75 to 23V output 1 to 17V adjustable. Available from ebay and the like.
